// Digital circuit ADDPG 1 bits (q3.3).dig as structural Verilog
module ADDPG_1_bits__q3_3 (
  input  A0,
  input  A1,
  input  Cin,
  output S,
  output P,
  output G
);

  wire xor_1_out;

  xor xor_1 (xor_1_out, A0, Cin);
  and and_1 (G, A0, A1);
  or or_1 (P, A0, A1);
  xor xor_2 (S, A1, xor_1_out);
endmodule
