// Digital circuit ADDPG 8 bitsd.dig as structural Verilog
module ADDPG_8_bitsd (
  input  A0,
  input  B0,
  input  A1,
  input  B1,
  input  A2,
  input  B2,
  input  A3,
  input  B3,
  input  A4,
  input  B4,
  input  A5,
  input  B5,
  input  A6,
  input  B6,
  input  A7,
  input  B7,
  input  CIn,
  output S0,
  output S1,
  output S2,
  output S3,
  output S4,
  output S5,
  output S6,
  output S7,
  output C7
);

  wire addpg_1_bits__q3_3_1_g, addpg_1_bits__q3_3_1_p, addpg_1_bits__q3_3_2_g, addpg_1_bits__q3_3_2_p,
       addpg_1_bits__q3_3_3_g, addpg_1_bits__q3_3_3_p, cc_8_bits__q3_4_1_p6, cc_8_bits__q3_4_1_p8,
       cc_8_bits__q3_4_1_p10, cc_8_bits__q3_4_1_p11, cc_8_bits__q3_4_1_p12, cc_8_bits__q3_4_1_p13,
       cc_8_bits__q3_4_1_p14, cc_8_bits__q3_4_1_p15, cc_8_bits__q3_4_1_p16, cc_8_bits__q3_4_1_p17,
       cc_8_bits__q3_4_1_p18, cc_8_bits__q3_4_1_p19, cc_8_bits__q3_4_1_p20, cc_8_bits__q3_4_1_p21,
       cc_8_bits__q3_4_1_p22, cc_8_bits__q3_4_1_p23, undriven;

  ADDPG_1_bits__q3_3 addpg_1_bits__q3_3_1 (
    .A0(A7), .A1(B7), .Cin(cc_8_bits__q3_4_1_p6), .S(S7), .P(addpg_1_bits__q3_3_1_p),
    .G(addpg_1_bits__q3_3_1_g));
  ADDPG_1_bits__q3_3 addpg_1_bits__q3_3_2 (
    .A0(A6), .A1(B6), .Cin(cc_8_bits__q3_4_1_p8), .S(S6), .P(addpg_1_bits__q3_3_2_p),
    .G(addpg_1_bits__q3_3_2_g));
  ADDPG_1_bits__q3_3 addpg_1_bits__q3_3_3 (
    .A0(A5), .A1(B5), .Cin(cc_8_bits__q3_4_1_p12), .S(S5), .P(addpg_1_bits__q3_3_3_p),
    .G(addpg_1_bits__q3_3_3_g));
  // CC_8_BIts__q3_4 cc_8_bits__q3_4_1: pin names not known; wires that end beside it: addpg_1_bits__q3_3_1_p, C7, addpg_1_bits__q3_3_1_g, addpg_1_bits__q3_3_2_p, addpg_1_bits__q3_3_2_g, cc_8_bits__q3_4_1_p6, addpg_1_bits__q3_3_3_p, cc_8_bits__q3_4_1_p8, addpg_1_bits__q3_3_3_g, cc_8_bits__q3_4_1_p10, cc_8_bits__q3_4_1_p11, cc_8_bits__q3_4_1_p12, cc_8_bits__q3_4_1_p13, cc_8_bits__q3_4_1_p14, cc_8_bits__q3_4_1_p15, cc_8_bits__q3_4_1_p16, cc_8_bits__q3_4_1_p17, cc_8_bits__q3_4_1_p18, cc_8_bits__q3_4_1_p19, cc_8_bits__q3_4_1_p20, cc_8_bits__q3_4_1_p21, cc_8_bits__q3_4_1_p22, cc_8_bits__q3_4_1_p23
  ADDPG_1_bits__q3_3 addpg_1_bits__q3_3_4 (
    .A0(A4), .A1(B4), .Cin(cc_8_bits__q3_4_1_p14), .S(S4), .P(cc_8_bits__q3_4_1_p10),
    .G(cc_8_bits__q3_4_1_p11));
  ADDPG_1_bits__q3_3 addpg_1_bits__q3_3_5 (
    .A0(A3), .A1(B3), .Cin(cc_8_bits__q3_4_1_p18), .S(S3), .P(cc_8_bits__q3_4_1_p13),
    .G(cc_8_bits__q3_4_1_p15));
  ADDPG_1_bits__q3_3 addpg_1_bits__q3_3_6 (
    .A0(A2), .A1(B2), .Cin(cc_8_bits__q3_4_1_p20), .S(S2), .P(cc_8_bits__q3_4_1_p16),
    .G(cc_8_bits__q3_4_1_p17));
  ADDPG_1_bits__q3_3 addpg_1_bits__q3_3_7 (
    .A0(A1), .A1(B1), .Cin(undriven), .S(S1), .P(cc_8_bits__q3_4_1_p19), .G(cc_8_bits__q3_4_1_p21));
  ADDPG_1_bits__q3_3 addpg_1_bits__q3_3_8 (
    .A0(A0), .A1(B0), .Cin(CIn), .S(S0), .P(cc_8_bits__q3_4_1_p22), .G(cc_8_bits__q3_4_1_p23));
endmodule
