// Digital circuit Bascule D clock.dig as structural Verilog
module Bascule_D_clock (
  input  D,
  input  CLK,
  input  w,
  output Q,
  output Q_2
);

  wire nand_1_out, nand_2_out;

  nand nand_1 (nand_1_out, D, w);
  nand nand_2 (nand_2_out, nand_1_out, w);
  nand nand_3 (Q, nand_1_out, Q_2);
  nand nand_4 (Q_2, Q, nand_2_out);
endmodule
