// Digital circuit CC 8 BIts (q3.4).dig as structural Verilog
module CC_8_BIts__q3_4 (
  input  G0,
  input  P0,
  input  P1,
  input  G1,
  input  P2,
  input  G2,
  input  P3,
  input  G3,
  input  P4,
  input  G4,
  input  P5,
  input  G5,
  input  P6,
  input  G6,
  input  P7,
  input  G7,
  input  Cin,
  output C0,
  output C1,
  output C2,
  output C3,
  output C4,
  output C5,
  output C6,
  output C7
);

  CC_1_bit cc_1_bit_1 (.G(G7), .P(P7), .Cin(C6), .Cout(C7));
  CC_1_bit cc_1_bit_2 (.G(G6), .P(P6), .Cin(C5), .Cout(C6));
  CC_1_bit cc_1_bit_3 (.G(G5), .P(P5), .Cin(C4), .Cout(C5));
  CC_1_bit cc_1_bit_4 (.G(G4), .P(P4), .Cin(C3), .Cout(C4));
  CC_1_bit cc_1_bit_5 (.G(G3), .P(P3), .Cin(C2), .Cout(C3));
  CC_1_bit cc_1_bit_6 (.G(G2), .P(P2), .Cin(C1), .Cout(C2));
  CC_1_bit cc_1_bit_7 (.G(G1), .P(P1), .Cin(C0), .Cout(C1));
  CC_1_bit cc_1_bit_8 (.G(G0), .P(P0), .Cin(Cin), .Cout(C0));
endmodule
