// Digital circuit Compteur 2.1 bis.dig as structural Verilog
module Compteur_2_1_bis (
  input  w,
  input  reset,
  output s0,
  output s1,
  output s2
);

  wire and_1_out, nor_1_out, not_1_out, or_1_out, or_2_out, xor_1_out, xor_2_out;

  and and_1 (and_1_out, s0, s1);
  xor xor_1 (xor_1_out, s0, s1);
  not not_1 (not_1_out, s0);
  xor xor_2 (xor_2_out, s2, and_1_out);
  nor nor_1 (nor_1_out, not_1_out, reset);
  or or_1 (or_1_out, xor_1_out, reset);
  D_FF_AS d_ff_as_1 ();  // open: Set, D, C, Clr, Q, nQ
  D_FF d_ff_1 (.D(nor_1_out), .C(w), .Q(s0));  // open: nQ
  D_FF d_ff_2 (.D(or_1_out), .C(w), .Q(s1));  // open: nQ
  D_FF d_ff_3 (.D(or_2_out), .C(w), .Q(s2));  // open: nQ
  or or_2 (or_2_out, xor_2_out, reset);
endmodule
