// Digital circuit MUX 4 to 1.dig as structural Verilog
module MUX_4_to_1 (
  input  A,
  input  B,
  input  C,
  input  D,
  input  C1,
  input  C0,
  output S
);

  wire and_1_out, and_2_out, and_3_out, and_4_out, and_5_out, and_6_out, and_7_out, and_8_out, not_1_out,
       not_2_out, not_3_out, not_4_out, or_1_out, or_2_out;

  not not_1 (not_1_out, C1);
  not not_2 (not_2_out, C0);
  not not_3 (not_3_out, C1);
  not not_4 (not_4_out, C0);
  and and_1 (and_1_out, C1, C0);
  and and_2 (and_2_out, not_1_out, not_2_out);
  and and_3 (and_3_out, not_3_out, C0);
  and and_4 (and_4_out, C1, not_4_out);
  and and_5 (and_5_out, and_2_out, A);
  and and_6 (and_6_out, and_3_out, B);
  and and_7 (and_7_out, and_4_out, C);
  and and_8 (and_8_out, and_1_out, D);
  or or_1 (or_1_out, and_5_out, and_6_out);
  or or_2 (or_2_out, and_7_out, and_8_out);
  or or_3 (S, or_1_out, or_2_out);
endmodule
