// Digital circuit Registre (q.1.1).dig as structural Verilog
module Registre__q_1_1 (
  input  D0,
  input  D1,
  input  D2,
  input  D3,
  input  D4,
  input  D5,
  input  D6,
  input  D7,
  input  CLK,
  output Q0,
  output Q1,
  output Q2,
  output Q3,
  output Q4,
  output Q5,
  output Q6,
  output Q7
);

  D_FF d_ff_1 (.D(D7), .C(CLK), .Q(Q7));  // open: nQ
  D_FF d_ff_2 (.D(D6), .C(CLK), .Q(Q6));  // open: nQ
  D_FF d_ff_3 (.D(D5), .C(CLK), .Q(Q5));  // open: nQ
  D_FF d_ff_4 (.D(D4), .C(CLK), .Q(Q4));  // open: nQ
  D_FF d_ff_5 (.D(D3), .C(CLK), .Q(Q3));  // open: nQ
  D_FF d_ff_6 (.D(D2), .C(CLK), .Q(Q2));  // open: nQ
  D_FF d_ff_7 (.D(D1), .C(CLK), .Q(Q1));  // open: nQ
  D_FF d_ff_8 (.D(D0), .C(CLK), .Q(Q0));  // open: nQ
endmodule
