// Digital circuit Registre à gauche 8b pour q3.1.dig as structural Verilog
module \Registre_à_gauche_8b_pour_q3_1  (
  input  e0,
  input  e1,
  input  e2,
  input  e3,
  input  e4,
  input  e5,
  input  e6,
  input  e7,
  input  DEC,
  input  w,
  output S0,
  output S1,
  output S2,
  output S3,
  output S4,
  output S5,
  output S6,
  output S7
);

  wire multiplexer_1_out, multiplexer_2_out, multiplexer_3_out, multiplexer_4_out, multiplexer_5_out,
       multiplexer_6_out, multiplexer_7_out, multiplexer_8_out, not_1_out;

  not not_1 (not_1_out, DEC);
  Multiplexer multiplexer_1 (.sel(not_1_out), .in_0(1'b0), .in_1(e0), .out(multiplexer_1_out));
  Multiplexer multiplexer_2 (.sel(not_1_out), .in_0(S0), .in_1(e1), .out(multiplexer_2_out));
  Multiplexer multiplexer_3 (.sel(not_1_out), .in_0(S1), .in_1(e2), .out(multiplexer_3_out));
  Multiplexer multiplexer_4 (.sel(not_1_out), .in_0(S2), .in_1(e3), .out(multiplexer_4_out));
  Multiplexer multiplexer_5 (.sel(not_1_out), .in_0(S3), .in_1(e4), .out(multiplexer_5_out));
  Multiplexer multiplexer_6 (.sel(not_1_out), .in_0(S4), .in_1(e5), .out(multiplexer_6_out));
  Multiplexer multiplexer_7 (.sel(not_1_out), .in_0(S5), .in_1(e6), .out(multiplexer_7_out));
  Multiplexer multiplexer_8 (.sel(not_1_out), .in_0(S6), .in_1(e7), .out(multiplexer_8_out));
  D_FF d_ff_1 (.D(multiplexer_1_out), .C(w), .Q(S0));  // open: nQ
  D_FF d_ff_2 (.D(multiplexer_2_out), .C(w), .Q(S1));  // open: nQ
  D_FF d_ff_3 (.D(multiplexer_3_out), .C(w), .Q(S2));  // open: nQ
  D_FF d_ff_4 (.D(multiplexer_4_out), .C(w), .Q(S3));  // open: nQ
  D_FF d_ff_5 (.D(multiplexer_5_out), .C(w), .Q(S4));  // open: nQ
  D_FF d_ff_6 (.D(multiplexer_6_out), .C(w), .Q(S5));  // open: nQ
  D_FF d_ff_7 (.D(multiplexer_7_out), .C(w), .Q(S6));  // open: nQ
  D_FF d_ff_8 (.D(multiplexer_8_out), .C(w), .Q(S7));  // open: nQ
endmodule
