// Digital circuit 2.1.dig as structural Verilog
module _2_1 (
);

  wire banc_de_registres_1_p1, banc_de_registres_1_p7, driver_3_out, exo1_1_1_p3;
  wire [4:0] IR__p_129_q_2;
  wire [31:0] add_1_s, banc_de_registres_1_p8, driver_1_out, IR__p_129_q, MAR_q, MDR_q, multiplexer_2_out,
       multiplexer_3_out, PC_q, SE_q, undriven;

  Driver driver_1 (.in(undriven[0]), .out(driver_1_out[0]));  // open: en
  Register #(.Bits(32)) PC (.D(undriven), .Q(PC_q));  // open: C, en
  Multiplexer #(.Bits(32)) multiplexer_1 (.in_0(add_1_s), .out(PC_q));  // open: sel, in_1
  Add #(.Bits(32)) add_1 (.a(undriven), .b(32'h4), .s(add_1_s));  // open: c_i, c_o
  Register #(.Bits(32)) IR__p_129 (
    .D(driver_1_out), .Q({IR__p_129_q[31:17], IR__p_129_q_2, IR__p_129_q[11:0]}));  // open: C, en
  Register #(.Bits(32)) MAR (.D(driver_1_out), .Q(MAR_q));  // open: C, en
  Register #(.Bits(32)) SE (.Q(SE_q));  // open: D, C, en
  // Banc_De_Registres banc_de_registres_1: pin names not known; wires that end beside it: banc_de_registres_1_p1, banc_de_registres_1_p1, IR__p_129_q[24:20], IR__p_129_q_2, IR__p_129_q[11:7], driver_1_out, banc_de_registres_1_p7, banc_de_registres_1_p8
  Multiplexer #(.Bits(32)) multiplexer_2 (
    .sel(SE_q[0]), .in_0(banc_de_registres_1_p8), .out(multiplexer_2_out));  // open: in_1
  Driver driver_2 (.in(banc_de_registres_1_p7), .out(driver_1_out[0]));  // open: en
  // exo1_1 exo1_1_1: pin names not known; wires that end beside it: banc_de_registres_1_p7, multiplexer_2_out, exo1_1_1_p3
  Driver driver_3 (.in(MDR_q[0]), .out(driver_3_out));  // open: en
  Multiplexer multiplexer_3 (.in_0(driver_1_out[0]), .in_1(driver_3_out), .out(multiplexer_3_out[0]));  // open: sel
  Register #(.Bits(32)) MDR (.D(multiplexer_3_out), .Q(MDR_q));  // open: C, en
  Driver driver_4 (.in(MDR_q[0]), .out(driver_1_out[0]));  // open: en
  Driver driver_5 (.in(exo1_1_1_p3), .out(driver_1_out[0]));  // open: en
  Register #(.Bits(32)) register_1 ();  // open: D, C, en, Q
  // Pins of 1 and 32 bits meet at SE_q
  // Pins of 1 and 32 bits meet at driver_1_out
  // Pins of 1 and 32 bits meet at multiplexer_3_out
  // Pins of 1 and 32 bits meet at MDR_q
  // Pins of 1 and 32 bits meet at undriven
endmodule
