// Digital circuit exo1.1.dig as structural Verilog
module exo1_1 (
  input  [31:0] A,
  input  [31:0] B,
  input  sub,
  input  [2:0] select,
  output [31:0] S,
  output cout
);

  wire [31:0] add_1_s, and_1_out, or_1_out, xor_1_out, xor_2_out;

  assign xor_1_out = B ^ {32{sub}};  // XOr xor_1, 32 bits wide
  assign or_1_out = A | B;  // Or or_1, 32 bits wide
  assign and_1_out = A & B;  // And and_1, 32 bits wide
  assign xor_2_out = A ^ B;  // XOr xor_2, 32 bits wide
  Add #(.Bits(32)) add_1 (.a(A), .b(xor_1_out), .c_i(sub), .s(add_1_s), .c_o(cout));
  Multiplexer #(.Bits(32), .Selector_Bits(3)) multiplexer_1 (
    .sel(select), .in_0(add_1_s), .in_1({32{1'b0}}), .in_2({32{1'b0}}), .in_3({32{1'b0}}), .in_4(xor_2_out),
    .in_5({32{1'b0}}), .in_6(or_1_out), .in_7(and_1_out), .out(S));
endmodule
