// Digital circuit exo1.2.dig as structural Verilog
module exo1_2 (
  input  [31:0] RES,
  input  [2:0] Rd,
  input  [2:0] Rs1,
  input  [2:0] Rs2,
  input  w_reg,
  output [31:0] src1,
  output [31:0] src2
);

  wire and_1_out, and_2_out, and_3_out, and_4_out, and_5_out, and_6_out, and_7_out, and_8_out, and_9_out,
       and_10_out, and_11_out, and_12_out, and_13_out, and_14_out, and_15_out, and_16_out, and_17_out,
       and_18_out, and_19_out, and_20_out, and_21_out, and_22_out, and_23_out, and_24_out, and_25_out,
       and_26_out, and_27_out, and_28_out, and_29_out, and_30_out, and_31_out, and_32_out, decoder_1_out_0,
       decoder_1_out_1, decoder_1_out_2, decoder_1_out_3, decoder_1_out_4, decoder_1_out_5, decoder_1_out_6,
       decoder_1_out_7, decoder_1_out_8, decoder_1_out_9, decoder_1_out_10, decoder_1_out_11,
       decoder_1_out_12, decoder_1_out_13, decoder_1_out_14, decoder_1_out_15, decoder_1_out_16,
       decoder_1_out_17, decoder_1_out_18, decoder_1_out_19, decoder_1_out_20, decoder_1_out_21,
       decoder_1_out_22, decoder_1_out_23, decoder_1_out_24, decoder_1_out_25, decoder_1_out_26,
       decoder_1_out_27, decoder_1_out_28, decoder_1_out_29, decoder_1_out_30, decoder_1_out_31,
       decoder_2_out_0, decoder_2_out_1, decoder_2_out_2, decoder_2_out_3, decoder_2_out_4, decoder_2_out_5,
       decoder_2_out_6, decoder_2_out_7, decoder_2_out_8, decoder_2_out_9, decoder_2_out_11,
       decoder_2_out_12, decoder_2_out_13, decoder_2_out_14, decoder_2_out_15, decoder_2_out_16,
       decoder_2_out_17, decoder_2_out_18, decoder_2_out_19, decoder_2_out_20, decoder_2_out_21,
       decoder_2_out_22, decoder_2_out_23, decoder_2_out_24, decoder_2_out_25, decoder_2_out_26,
       decoder_2_out_27, decoder_2_out_28, decoder_2_out_29, decoder_2_out_30, decoder_2_out_31,
       decoder_3_out_0, decoder_3_out_1, decoder_3_out_2, decoder_3_out_3, decoder_3_out_4, decoder_3_out_5,
       decoder_3_out_6, decoder_3_out_8, decoder_3_out_9, decoder_3_out_10, decoder_3_out_11,
       decoder_3_out_12, decoder_3_out_13, decoder_3_out_14, decoder_3_out_15, decoder_3_out_16,
       decoder_3_out_17, decoder_3_out_18, decoder_3_out_19, decoder_3_out_20, decoder_3_out_21,
       decoder_3_out_22, decoder_3_out_23, decoder_3_out_24, decoder_3_out_25, decoder_3_out_26,
       decoder_3_out_27, decoder_3_out_28, decoder_3_out_29, decoder_3_out_30, decoder_3_out_31, undriven,
       undriven_2, undriven_3, undriven_4;
  wire [31:0] D0_q, D1_q, D2_q, D3_q, D4_q, D5_q, D6_q, D7_q, D8_q, D9_q, D11_q, D12_q, D13_q, D14_q, D15_q,
       D16_q, D17_q, D19_q, D20_q, D21_q, D22_q, D23_q, D24_q, D25_q, D26_q, D27_q, D28_q, D30_q, D31_q,
       decoder_2_out_10, decoder_3_out_7, driver_1_out, driver_19_out, undriven_5, undriven_6, undriven_7,
       undriven_8, undriven_9, undriven_10;

  Decoder #(.Selector_Bits(5)) decoder_1 (
    .out_0(decoder_1_out_0), .out_1(decoder_1_out_1), .out_2(decoder_1_out_2), .out_3(decoder_1_out_3),
    .out_4(decoder_1_out_4), .out_5(decoder_1_out_5), .out_6(decoder_1_out_6), .out_7(decoder_1_out_7),
    .out_8(decoder_1_out_8), .out_9(decoder_1_out_9), .out_10(decoder_1_out_10), .out_11(decoder_1_out_11),
    .out_12(decoder_1_out_12), .out_13(decoder_1_out_13), .out_14(decoder_1_out_14),
    .out_15(decoder_1_out_15), .out_16(decoder_1_out_16), .out_17(decoder_1_out_17),
    .out_18(decoder_1_out_18), .out_19(decoder_1_out_19), .out_20(decoder_1_out_20),
    .out_21(decoder_1_out_21), .out_22(decoder_1_out_22), .out_23(decoder_1_out_23),
    .out_24(decoder_1_out_24), .out_25(decoder_1_out_25), .out_26(decoder_1_out_26),
    .out_27(decoder_1_out_27), .out_28(decoder_1_out_28), .out_29(decoder_1_out_29),
    .out_30(decoder_1_out_30), .out_31(decoder_1_out_31));  // open: sel
  and and_1 (and_1_out, decoder_1_out_0, undriven_4);
  and and_2 (and_2_out, decoder_1_out_1, undriven_4);
  and and_3 (and_3_out, decoder_1_out_2, undriven_4);
  and and_4 (and_4_out, decoder_1_out_3, undriven_4);
  and and_5 (and_5_out, decoder_1_out_4, undriven_4);
  and and_6 (and_6_out, decoder_1_out_5, undriven_4);
  and and_7 (and_7_out, decoder_1_out_6, undriven_4);
  and and_8 (and_8_out, decoder_1_out_7, undriven_4);
  and and_9 (and_9_out, decoder_1_out_8, undriven);
  and and_10 (and_10_out, decoder_1_out_9, undriven);
  and and_11 (and_11_out, decoder_1_out_10, undriven);
  and and_12 (and_12_out, decoder_1_out_11, undriven);
  and and_13 (and_13_out, decoder_1_out_12, undriven);
  and and_14 (and_14_out, decoder_1_out_13, undriven);
  and and_15 (and_15_out, decoder_1_out_14, undriven);
  and and_16 (and_16_out, decoder_1_out_15, undriven);
  and and_17 (and_17_out, decoder_1_out_16, undriven_3);
  and and_18 (and_18_out, decoder_1_out_17, undriven_3);
  and and_19 (and_19_out, decoder_1_out_18, undriven_3);
  and and_20 (and_20_out, decoder_1_out_19, undriven_3);
  and and_21 (and_21_out, decoder_1_out_20, undriven_3);
  and and_22 (and_22_out, decoder_1_out_21, undriven_3);
  and and_23 (and_23_out, decoder_1_out_22, undriven_3);
  and and_24 (and_24_out, decoder_1_out_23, undriven_3);
  and and_25 (and_25_out, decoder_1_out_24, undriven_2);
  and and_26 (and_26_out, decoder_1_out_25, undriven_2);
  and and_27 (and_27_out, decoder_1_out_26, undriven_2);
  and and_28 (and_28_out, decoder_1_out_27, undriven_2);
  and and_29 (and_29_out, decoder_1_out_28, undriven_2);
  and and_30 (and_30_out, decoder_1_out_29, undriven_2);
  and and_31 (and_31_out, decoder_1_out_30, undriven_2);
  and and_32 (and_32_out, decoder_1_out_31, undriven_2);
  D_FF #(.Bits(32)) D0 (.D(undriven_10), .C(and_1_out), .Q(D0_q));  // open: nQ
  D_FF #(.Bits(32)) D1 (.D(undriven_10), .C(and_2_out), .Q(D1_q));  // open: nQ
  D_FF #(.Bits(32)) D2 (.D(undriven_10), .C(and_3_out), .Q(D2_q));  // open: nQ
  D_FF #(.Bits(32)) D3 (.D(undriven_10), .C(and_4_out), .Q(D3_q));  // open: nQ
  D_FF #(.Bits(32)) D4 (.D(undriven_10), .C(and_5_out), .Q(D4_q));  // open: nQ
  D_FF #(.Bits(32)) D5 (.D(undriven_10), .C(and_6_out), .Q(D5_q));  // open: nQ
  D_FF #(.Bits(32)) D6 (.D(undriven_10), .C(and_7_out), .Q(D6_q));  // open: nQ
  D_FF #(.Bits(32)) D7 (.D(undriven_10), .C(and_8_out), .Q(D7_q));  // open: nQ
  D_FF #(.Bits(32)) D8 (.D(undriven_5), .C(and_9_out), .Q(D8_q));  // open: nQ
  D_FF #(.Bits(32)) D9 (.D(undriven_5), .C(and_10_out), .Q(D9_q));  // open: nQ
  D_FF #(.Bits(32)) D10 (.D(undriven_5), .C(and_11_out));  // open: Q, nQ
  D_FF #(.Bits(32)) D11 (.D(undriven_5), .C(and_12_out), .Q(D11_q));  // open: nQ
  D_FF #(.Bits(32)) D12 (.D(undriven_5), .C(and_13_out), .Q(D12_q));  // open: nQ
  D_FF #(.Bits(32)) D13 (.D(undriven_5), .C(and_14_out), .Q(D13_q));  // open: nQ
  D_FF #(.Bits(32)) D14 (.D(undriven_5), .C(and_15_out), .Q(D14_q));  // open: nQ
  D_FF #(.Bits(32)) D15 (.D(undriven_5), .C(and_16_out), .Q(D15_q));  // open: nQ
  D_FF #(.Bits(32)) D16 (.D(undriven_7), .C(and_17_out), .Q(D16_q));  // open: nQ
  D_FF #(.Bits(32)) D17 (.D(undriven_7), .C(and_18_out), .Q(D17_q));  // open: nQ
  D_FF #(.Bits(32)) D18 (.D(undriven_7), .C(and_19_out));  // open: Q, nQ
  D_FF #(.Bits(32)) D19 (.D(undriven_7), .C(and_20_out), .Q(D19_q));  // open: nQ
  D_FF #(.Bits(32)) D20 (.D(undriven_7), .C(and_21_out), .Q(D20_q));  // open: nQ
  D_FF #(.Bits(32)) D21 (.D(undriven_7), .C(and_22_out), .Q(D21_q));  // open: nQ
  D_FF #(.Bits(32)) D22 (.D(undriven_7), .C(and_23_out), .Q(D22_q));  // open: nQ
  D_FF #(.Bits(32)) D23 (.D(undriven_7), .C(and_24_out), .Q(D23_q));  // open: nQ
  D_FF #(.Bits(32)) D24 (.D(undriven_6), .C(and_25_out), .Q(D24_q));  // open: nQ
  D_FF #(.Bits(32)) D25 (.D(undriven_6), .C(and_26_out), .Q(D25_q));  // open: nQ
  D_FF #(.Bits(32)) D26 (.D(undriven_6), .C(and_27_out), .Q(D26_q));  // open: nQ
  D_FF #(.Bits(32)) D27 (.D(undriven_6), .C(and_28_out), .Q(D27_q));  // open: nQ
  D_FF #(.Bits(32)) D28 (.D(undriven_6), .C(and_29_out), .Q(D28_q));  // open: nQ
  D_FF #(.Bits(32)) D29 (.D(undriven_6), .C(and_30_out));  // open: Q, nQ
  D_FF #(.Bits(32)) D30 (.D(undriven_6), .C(and_31_out), .Q(D30_q));  // open: nQ
  D_FF #(.Bits(32)) D31 (.D(undriven_6), .C(and_32_out), .Q(D31_q));  // open: nQ
  Decoder #(.Selector_Bits(5)) decoder_2 (
    .out_0(decoder_2_out_0), .out_1(decoder_2_out_1), .out_2(decoder_2_out_2), .out_3(decoder_2_out_3),
    .out_4(decoder_2_out_4), .out_5(decoder_2_out_5), .out_6(decoder_2_out_6), .out_7(decoder_2_out_7),
    .out_8(decoder_2_out_8), .out_9(decoder_2_out_9), .out_10(decoder_2_out_10[0]),
    .out_11(decoder_2_out_11), .out_12(decoder_2_out_12), .out_13(decoder_2_out_13),
    .out_14(decoder_2_out_14), .out_15(decoder_2_out_15), .out_16(decoder_2_out_16),
    .out_17(decoder_2_out_17), .out_18(decoder_2_out_18), .out_19(decoder_2_out_19),
    .out_20(decoder_2_out_20), .out_21(decoder_2_out_21), .out_22(decoder_2_out_22),
    .out_23(decoder_2_out_23), .out_24(decoder_2_out_24), .out_25(decoder_2_out_25),
    .out_26(decoder_2_out_26), .out_27(decoder_2_out_27), .out_28(decoder_2_out_28),
    .out_29(decoder_2_out_29), .out_30(decoder_2_out_30), .out_31(decoder_2_out_31));  // open: sel
  assign driver_1_out = decoder_2_out_0 ? D0_q : 32'bz;  // Driver driver_1
  assign driver_1_out = decoder_2_out_1 ? D1_q : 32'bz;  // Driver driver_2
  assign driver_1_out = decoder_2_out_2 ? D2_q : 32'bz;  // Driver driver_3
  assign driver_1_out = decoder_2_out_3 ? D3_q : 32'bz;  // Driver driver_4
  assign driver_1_out = decoder_2_out_4 ? D4_q : 32'bz;  // Driver driver_5
  assign driver_1_out = decoder_2_out_5 ? D5_q : 32'bz;  // Driver driver_6
  assign driver_1_out = decoder_2_out_6 ? D6_q : 32'bz;  // Driver driver_7
  assign driver_1_out = decoder_2_out_7 ? D7_q : 32'bz;  // Driver driver_8
  assign driver_1_out = decoder_2_out_8 ? D8_q : 32'bz;  // Driver driver_9
  assign driver_1_out = decoder_2_out_9 ? D9_q : 32'bz;  // Driver driver_10
  Driver #(.Bits(32)) driver_11 (.in(decoder_2_out_10), .out(driver_1_out));  // open: en
  assign driver_1_out = decoder_2_out_11 ? D11_q : 32'bz;  // Driver driver_12
  assign driver_1_out = decoder_2_out_12 ? D12_q : 32'bz;  // Driver driver_13
  assign driver_1_out = decoder_2_out_13 ? D13_q : 32'bz;  // Driver driver_14
  assign driver_1_out = decoder_2_out_14 ? D14_q : 32'bz;  // Driver driver_15
  assign driver_1_out = decoder_2_out_15 ? D15_q : 32'bz;  // Driver driver_16
  assign driver_1_out = decoder_2_out_16 ? D16_q : 32'bz;  // Driver driver_17
  assign driver_1_out = decoder_2_out_17 ? D17_q : 32'bz;  // Driver driver_18
  assign driver_19_out = decoder_3_out_0 ? D0_q : 32'bz;  // Driver driver_19
  assign driver_1_out = decoder_2_out_18 ? undriven_9 : 32'bz;  // Driver driver_20
  assign driver_1_out = decoder_2_out_19 ? D19_q : 32'bz;  // Driver driver_21
  assign driver_19_out = decoder_3_out_1 ? D1_q : 32'bz;  // Driver driver_22
  assign driver_19_out = decoder_3_out_2 ? D2_q : 32'bz;  // Driver driver_23
  assign driver_19_out = decoder_3_out_3 ? D3_q : 32'bz;  // Driver driver_24
  assign driver_1_out = decoder_2_out_20 ? D20_q : 32'bz;  // Driver driver_25
  assign driver_1_out = decoder_2_out_21 ? D21_q : 32'bz;  // Driver driver_26
  assign driver_19_out = decoder_3_out_4 ? D4_q : 32'bz;  // Driver driver_27
  assign driver_1_out = decoder_2_out_22 ? D22_q : 32'bz;  // Driver driver_28
  assign driver_19_out = decoder_3_out_5 ? D5_q : 32'bz;  // Driver driver_29
  assign driver_19_out = decoder_3_out_6 ? D6_q : 32'bz;  // Driver driver_30
  assign driver_19_out = decoder_3_out_7[0] ? D7_q : 32'bz;  // Driver driver_31
  assign driver_1_out = decoder_2_out_23 ? D23_q : 32'bz;  // Driver driver_32
  assign driver_1_out = decoder_2_out_24 ? D24_q : 32'bz;  // Driver driver_33
  assign driver_19_out = decoder_3_out_8 ? D8_q : 32'bz;  // Driver driver_34
  assign driver_19_out = decoder_3_out_9 ? D9_q : 32'bz;  // Driver driver_35
  assign driver_19_out = decoder_3_out_10 ? decoder_2_out_10 : 32'bz;  // Driver driver_36
  assign driver_19_out = decoder_3_out_11 ? decoder_3_out_7 : 32'bz;  // Driver driver_37
  assign driver_1_out = decoder_2_out_25 ? D25_q : 32'bz;  // Driver driver_38
  Driver #(.Bits(32)) driver_39 (.in(D12_q), .en(decoder_3_out_12));  // open: out
  Driver #(.Bits(32)) driver_40 (.in(D13_q), .en(decoder_3_out_13));  // open: out
  assign driver_1_out = decoder_2_out_26 ? D26_q : 32'bz;  // Driver driver_41
  assign driver_1_out = decoder_2_out_27 ? D27_q : 32'bz;  // Driver driver_42
  Decoder #(.Selector_Bits(5)) decoder_3 (
    .out_0(decoder_3_out_0), .out_1(decoder_3_out_1), .out_2(decoder_3_out_2), .out_3(decoder_3_out_3),
    .out_4(decoder_3_out_4), .out_5(decoder_3_out_5), .out_6(decoder_3_out_6), .out_7(decoder_3_out_7[0]),
    .out_8(decoder_3_out_8), .out_9(decoder_3_out_9), .out_10(decoder_3_out_10), .out_11(decoder_3_out_11),
    .out_12(decoder_3_out_12), .out_13(decoder_3_out_13), .out_14(decoder_3_out_14),
    .out_15(decoder_3_out_15), .out_16(decoder_3_out_16), .out_17(decoder_3_out_17),
    .out_18(decoder_3_out_18), .out_19(decoder_3_out_19), .out_20(decoder_3_out_20),
    .out_21(decoder_3_out_21), .out_22(decoder_3_out_22), .out_23(decoder_3_out_23),
    .out_24(decoder_3_out_24), .out_25(decoder_3_out_25), .out_26(decoder_3_out_26),
    .out_27(decoder_3_out_27), .out_28(decoder_3_out_28), .out_29(decoder_3_out_29),
    .out_30(decoder_3_out_30), .out_31(decoder_3_out_31));  // open: sel
  Driver #(.Bits(32)) driver_43 (.in(D14_q), .en(decoder_3_out_14));  // open: out
  Driver #(.Bits(32)) driver_44 (.in(D15_q), .en(decoder_3_out_15));  // open: out
  assign driver_1_out = decoder_2_out_28 ? D28_q : 32'bz;  // Driver driver_45
  assign driver_1_out = decoder_2_out_29 ? undriven_8 : 32'bz;  // Driver driver_46
  Driver #(.Bits(32)) driver_47 (.in(D16_q), .en(decoder_3_out_16));  // open: out
  Driver #(.Bits(32)) driver_48 (.in(D17_q), .en(decoder_3_out_17));  // open: out
  assign driver_1_out = decoder_2_out_30 ? D30_q : 32'bz;  // Driver driver_49
  assign driver_1_out = decoder_2_out_31 ? D31_q : 32'bz;  // Driver driver_50
  Driver #(.Bits(32)) driver_51 (.in(undriven_9), .en(decoder_3_out_18));  // open: out
  Driver #(.Bits(32)) driver_52 (.in(D19_q), .en(decoder_3_out_19));  // open: out
  Driver #(.Bits(32)) driver_53 (.in(D20_q), .en(decoder_3_out_20));  // open: out
  Driver #(.Bits(32)) driver_54 (.in(D21_q), .en(decoder_3_out_21));  // open: out
  Driver #(.Bits(32)) driver_55 (.in(D22_q), .en(decoder_3_out_22));  // open: out
  Driver #(.Bits(32)) driver_56 (.in(D23_q), .en(decoder_3_out_23));  // open: out
  Driver #(.Bits(32)) driver_57 (.in(D24_q), .en(decoder_3_out_24));  // open: out
  Driver #(.Bits(32)) driver_58 (.in(D25_q), .en(decoder_3_out_25));  // open: out
  Driver #(.Bits(32)) driver_59 (.in(D26_q), .en(decoder_3_out_26));  // open: out
  Driver #(.Bits(32)) driver_60 (.in(D27_q), .en(decoder_3_out_27));  // open: out
  Driver #(.Bits(32)) driver_61 (.in(D28_q), .en(decoder_3_out_28));  // open: out
  Driver #(.Bits(32)) driver_62 (.in(D30_q), .en(decoder_3_out_29));  // open: out
  Driver #(.Bits(32)) driver_63 (.en(decoder_3_out_30));  // open: in, out
  Driver #(.Bits(32)) driver_64 (.in(D31_q), .en(decoder_3_out_31));  // open: out
  // Pins of 1 and 32 bits meet at decoder_2_out_10
  // Pins of 1 and 32 bits meet at decoder_3_out_7
endmodule
