// Digital circuit UAL.dig as structural Verilog
module UAL (
  input  [7:0] A,
  input  [7:0] B,
  input  SUB,
  input  C0,
  input  C1,
  output Cout,
  output S0,
  output S1,
  output S2,
  output S3,
  output S4,
  output S5,
  output S6,
  output S7
);

  wire add_sub_8_bits_1_s0, add_sub_8_bits_1_s1, add_sub_8_bits_1_s2, add_sub_8_bits_1_s3,
       add_sub_8_bits_1_s4, add_sub_8_bits_1_s5, add_sub_8_bits_1_s6, add_sub_8_bits_1_s7,
       and_bin__q5_3_1_s0, and_bin__q5_3_1_s1, and_bin__q5_3_1_s2, and_bin__q5_3_1_s3, and_bin__q5_3_1_s4,
       and_bin__q5_3_1_s5, and_bin__q5_3_1_s6, and_bin__q5_3_1_s7, or_bin__q5_2_1_s0, or_bin__q5_2_1_s1,
       or_bin__q5_2_1_s2, or_bin__q5_2_1_s3, or_bin__q5_2_1_s4, or_bin__q5_2_1_s5, or_bin__q5_2_1_s6,
       or_bin__q5_2_1_s7, xor_bin__q5_11_1_s0, xor_bin__q5_11_1_s1, xor_bin__q5_11_1_s2, xor_bin__q5_11_1_s3,
       xor_bin__q5_11_1_s4, xor_bin__q5_11_1_s5, xor_bin__q5_11_1_s6, xor_bin__q5_11_1_s7;

  MUX_4_to_1 mux_4_to_1_1 (
    .A(add_sub_8_bits_1_s7), .B(and_bin__q5_3_1_s7), .C(or_bin__q5_2_1_s7), .D(xor_bin__q5_11_1_s7), .C1(C1),
    .C0(C0), .S(S7));
  MUX_4_to_1 mux_4_to_1_2 (
    .A(add_sub_8_bits_1_s6), .B(and_bin__q5_3_1_s6), .C(or_bin__q5_2_1_s6), .D(xor_bin__q5_11_1_s6), .C1(C1),
    .C0(C0), .S(S6));
  MUX_4_to_1 mux_4_to_1_3 (
    .A(add_sub_8_bits_1_s5), .B(and_bin__q5_3_1_s5), .C(or_bin__q5_2_1_s5), .D(xor_bin__q5_11_1_s5), .C1(C1),
    .C0(C0), .S(S5));
  XOR_BIN__q5_11 xor_bin__q5_11_1 (
    .A(A), .B(B), .S0(xor_bin__q5_11_1_s0), .S1(xor_bin__q5_11_1_s1), .S2(xor_bin__q5_11_1_s2),
    .S3(xor_bin__q5_11_1_s3), .S4(xor_bin__q5_11_1_s4), .S5(xor_bin__q5_11_1_s5), .S6(xor_bin__q5_11_1_s6),
    .S7(xor_bin__q5_11_1_s7));
  MUX_4_to_1 mux_4_to_1_4 (
    .A(add_sub_8_bits_1_s4), .B(and_bin__q5_3_1_s4), .C(or_bin__q5_2_1_s4), .D(xor_bin__q5_11_1_s4), .C1(C1),
    .C0(C0), .S(S4));
  MUX_4_to_1 mux_4_to_1_5 (
    .A(add_sub_8_bits_1_s3), .B(and_bin__q5_3_1_s3), .C(or_bin__q5_2_1_s3), .D(xor_bin__q5_11_1_s3), .C1(C1),
    .C0(C0), .S(S3));
  OR_BIN__q5_2 or_bin__q5_2_1 (
    .A(A), .B(B), .S0(or_bin__q5_2_1_s0), .S1(or_bin__q5_2_1_s1), .S2(or_bin__q5_2_1_s2),
    .S3(or_bin__q5_2_1_s3), .S4(or_bin__q5_2_1_s4), .S5(or_bin__q5_2_1_s5), .S6(or_bin__q5_2_1_s6),
    .S7(or_bin__q5_2_1_s7));
  MUX_4_to_1 mux_4_to_1_6 (
    .A(add_sub_8_bits_1_s2), .B(and_bin__q5_3_1_s2), .C(or_bin__q5_2_1_s2), .D(xor_bin__q5_11_1_s2), .C1(C1),
    .C0(C0), .S(S2));
  AND_BIN__q5_3 and_bin__q5_3_1 (
    .A(A), .B(B), .S0(and_bin__q5_3_1_s0), .S1(and_bin__q5_3_1_s1), .S2(and_bin__q5_3_1_s2),
    .S3(and_bin__q5_3_1_s3), .S4(and_bin__q5_3_1_s4), .S5(and_bin__q5_3_1_s5), .S6(and_bin__q5_3_1_s6),
    .S7(and_bin__q5_3_1_s7));
  MUX_4_to_1 mux_4_to_1_7 (
    .A(add_sub_8_bits_1_s1), .B(and_bin__q5_3_1_s1), .C(or_bin__q5_2_1_s1), .D(xor_bin__q5_11_1_s1), .C1(C1),
    .C0(C0), .S(S1));
  ADD_SUB_8_bits add_sub_8_bits_1 (
    .Sub(SUB), .B(B), .A(A), .Cout(Cout), .S0(add_sub_8_bits_1_s0), .S1(add_sub_8_bits_1_s1),
    .S2(add_sub_8_bits_1_s2), .S3(add_sub_8_bits_1_s3), .S4(add_sub_8_bits_1_s4), .S5(add_sub_8_bits_1_s5),
    .S6(add_sub_8_bits_1_s6), .S7(add_sub_8_bits_1_s7));
  MUX_4_to_1 mux_4_to_1_8 (
    .A(add_sub_8_bits_1_s0), .B(and_bin__q5_3_1_s0), .C(or_bin__q5_2_1_s0), .D(xor_bin__q5_11_1_s0), .C1(C1),
    .C0(C0), .S(S0));
endmodule
