// Digital circuit circuit a saturation(q2.3).dig as structural Verilog
module circuit_a_saturation_q2_3 (
  input  INC,
  input  w,
  input  res,
  output s0,
  output s1,
  output s2
);

  wire and_1_out, and_2_out, and_3_out, and_4_out, and_5_out, and_6_out, and_7_out, and_8_out, and_9_out,
       and_10_out, d_ff_1_q, d_ff_2_q, d_ff_3_q, multiplexer_1_out, not_1_out, not_2_out, not_3_out,
       not_4_out, not_5_out, not_6_out, not_7_out, not_8_out, not_9_out, or_1_out, xor_1_out, xor_2_out;

  and and_1 (and_1_out, d_ff_1_q, d_ff_2_q);
  Multiplexer multiplexer_1 (.sel(or_1_out), .in_0(w), .in_1(1'b0), .out(multiplexer_1_out));
  not not_1 (not_1_out, res);
  not not_2 (not_2_out, d_ff_1_q);
  xor xor_1 (xor_1_out, d_ff_1_q, d_ff_2_q);
  xor xor_2 (xor_2_out, d_ff_3_q, and_1_out);
  D_FF d_ff_1 (.D(and_2_out), .C(multiplexer_1_out), .Q(d_ff_1_q));  // open: nQ
  D_FF d_ff_2 (.D(and_3_out), .C(multiplexer_1_out), .Q(d_ff_2_q));  // open: nQ
  D_FF d_ff_3 (.D(and_4_out), .C(multiplexer_1_out), .Q(d_ff_3_q));  // open: nQ
  and and_2 (and_2_out, not_2_out, not_1_out);
  and and_3 (and_3_out, xor_1_out, not_1_out);
  and and_4 (and_4_out, xor_2_out, not_1_out);
  not not_3 (not_3_out, d_ff_1_q);
  not not_4 (not_4_out, d_ff_2_q);
  not not_5 (not_5_out, d_ff_3_q);
  Multiplexer multiplexer_2 (.sel(INC), .in_0(not_3_out), .in_1(d_ff_1_q), .out(s0));
  Multiplexer multiplexer_3 (.sel(INC), .in_0(not_4_out), .in_1(d_ff_2_q), .out(s1));
  Multiplexer multiplexer_4 (.sel(INC), .in_0(not_5_out), .in_1(d_ff_3_q), .out(s2));
  and and_5 (and_5_out, s1, s0);
  and and_6 (and_6_out, s2, and_5_out);
  and and_7 (and_7_out, INC, and_6_out);
  or or_1 (or_1_out, and_10_out, and_7_out);
  not not_6 (not_6_out, s0);
  not not_7 (not_7_out, s1);
  and and_8 (and_8_out, not_7_out, not_6_out);
  not not_8 (not_8_out, s2);
  and and_9 (and_9_out, not_8_out, and_8_out);
  not not_9 (not_9_out, INC);
  and and_10 (and_10_out, and_9_out, not_9_out);
endmodule
