// Digital circuit compt n.dig as structural Verilog
module compt_n (
  input  w,
  input  res,
  output s0,
  output s1,
  output s2
);

  wire and_1_out, not_1_out, xor_1_out, xor_2_out;

  and and_1 (and_1_out, s0, s1);
  not not_1 (not_1_out, s0);
  xor xor_1 (xor_1_out, s0, s1);
  xor xor_2 (xor_2_out, s2, and_1_out);
  D_FF_AS d_ff_as_1 (.D(not_1_out), .C(w), .Clr(res), .Q(s0));  // open: Set, nQ
  D_FF_AS d_ff_as_2 (.D(xor_1_out), .C(w), .Clr(res), .Q(s1));  // open: Set, nQ
  D_FF_AS d_ff_as_3 (.D(xor_2_out), .C(w), .Clr(res), .Q(s2));  // open: Set, nQ
endmodule
