// Digital circuit compte decompte 2 officiel (q2.2).dig as structural Verilog
module compte_decompte_2_officiel__q2_2 (
  input  INC,
  input  w,
  input  res,
  output s0,
  output s1,
  output s2
);

  wire and_1_out, and_2_out, and_3_out, and_4_out, d_ff_1_q, d_ff_2_q, d_ff_3_q, not_1_out, not_2_out,
       not_3_out, not_4_out, not_5_out, xor_1_out, xor_2_out;

  and and_1 (and_1_out, d_ff_1_q, d_ff_2_q);
  not not_1 (not_1_out, res);
  xor xor_1 (xor_1_out, d_ff_1_q, d_ff_2_q);
  not not_2 (not_2_out, d_ff_1_q);
  xor xor_2 (xor_2_out, d_ff_3_q, and_1_out);
  D_FF d_ff_1 (.D(and_2_out), .C(w), .Q(d_ff_1_q));  // open: nQ
  D_FF d_ff_2 (.D(and_3_out), .C(w), .Q(d_ff_2_q));  // open: nQ
  D_FF d_ff_3 (.D(and_4_out), .C(w), .Q(d_ff_3_q));  // open: nQ
  and and_2 (and_2_out, not_2_out, not_1_out);
  and and_3 (and_3_out, xor_1_out, not_1_out);
  and and_4 (and_4_out, xor_2_out, not_1_out);
  not not_3 (not_3_out, d_ff_1_q);
  not not_4 (not_4_out, d_ff_2_q);
  not not_5 (not_5_out, d_ff_3_q);
  Multiplexer multiplexer_1 (.sel(INC), .in_0(not_3_out), .in_1(d_ff_1_q), .out(s0));
  Multiplexer multiplexer_2 (.sel(INC), .in_0(not_4_out), .in_1(d_ff_2_q), .out(s1));
  Multiplexer multiplexer_3 (.sel(INC), .in_0(not_5_out), .in_1(d_ff_3_q), .out(s2));
endmodule
