// Digital circuit compteur à 4 pour multi.dig as structural Verilog
module \compteur_à_4_pour_multi  (
  input  w,
  input  res,
  output s0,
  output s1
);

  wire and_1_out, and_2_out, d_ff_1_q, d_ff_2_q, not_1_out, not_2_out, xor_1_out;

  xor xor_1 (xor_1_out, d_ff_2_q, d_ff_1_q);
  not not_1 (not_1_out, res);
  not not_2 (not_2_out, d_ff_1_q);
  D_FF d_ff_1 (.D(and_1_out), .C(w), .Q(d_ff_1_q));  // open: nQ
  D_FF d_ff_2 (.D(and_2_out), .C(w), .Q(d_ff_2_q));  // open: nQ
  and and_1 (and_1_out, not_2_out, not_1_out);
  and and_2 (and_2_out, xor_1_out, not_1_out);
  not not_3 (s0, d_ff_1_q);
  not not_4 (s1, d_ff_2_q);
endmodule
