// Digital circuit deco 3-8.dig as structural Verilog
module deco_3_8 (
  input  e0,
  input  e1,
  input  e3,
  output y0,
  output y1,
  output y2,
  output y3,
  output y4,
  output y5,
  output y6,
  output y7
);

  wire and_1_out, and_2_out, and_3_out, and_4_out, not_1_out, not_2_out, not_3_out;

  not not_1 (not_1_out, e3);
  not not_2 (not_2_out, e1);
  and and_1 (and_1_out, not_1_out, not_2_out);
  and and_2 (and_2_out, not_1_out, e1);
  and and_3 (and_3_out, e3, not_2_out);
  and and_4 (and_4_out, e1, e3);
  not not_3 (not_3_out, e0);
  and and_5 (y0, and_1_out, not_3_out);
  and and_6 (y1, and_1_out, e0);
  and and_7 (y2, and_2_out, not_3_out);
  and and_8 (y3, and_2_out, e0);
  and and_9 (y4, and_3_out, not_3_out);
  and and_10 (y5, and_3_out, e0);
  and and_11 (y6, and_4_out, not_3_out);
  and and_12 (y7, and_4_out, e0);
endmodule
