// Digital circuit décodeur exo 2.dig as structural Verilog
module \décodeur_exo_2  (
  input  a1,
  input  a0,
  output y0,
  output y1,
  output y2,
  output y3
);

  wire not_1_out, not_2_out;

  not not_1 (not_1_out, a0);
  not not_2 (not_2_out, a1);
  and and_1 (y0, not_1_out, not_2_out);
  and and_2 (y1, not_1_out, a1);
  and and_3 (y2, a0, not_2_out);
  and and_4 (y3, a0, a1);
endmodule
