// Digital circuit gauche droite uppercut.dig as structural Verilog
module gauche_droite_uppercut (
  input  [7:0] E,
  input  DEC,
  input  w,
  input  LEFT,
  output Q0,
  output Q1,
  output Q2,
  output Q3,
  output Q4,
  output Q5,
  output Q6,
  output Q7
);

  wire multiplexer_1_out, multiplexer_3_out, multiplexer_7_out, multiplexer_10_out, multiplexer_12_out,
       multiplexer_14_out, multiplexer_15_out, multiplexer_16_out;

  Multiplexer multiplexer_1 (.sel(E[2]), .in_0(1'b0), .in_1(E[7]), .out(multiplexer_1_out));
  Multiplexer multiplexer_2 (.sel(LEFT), .in_0(E[0]), .in_1(Q6), .out(Q7));
  D_FF d_ff_1 (.D(multiplexer_1_out), .C(w), .Q(Q7));  // open: nQ
  not not_1 (E[2], DEC);
  Multiplexer multiplexer_3 (.sel(E[2]), .in_0(Q7), .in_1(E[6]), .out(multiplexer_3_out));
  D_FF d_ff_2 (.D(multiplexer_3_out), .C(w), .Q(Q6));  // open: nQ
  Multiplexer multiplexer_4 (.sel(LEFT), .in_0(E[1]), .in_1(w), .out(Q6));
  Multiplexer multiplexer_5 (.sel(E[2]), .in_0(Q6), .in_1(E[5]), .out(w));
  D_FF d_ff_3 (.D(w), .C(w), .Q(w));  // open: nQ
  Multiplexer multiplexer_6 (.sel(LEFT), .in_0(E[2]), .in_1(Q4), .out(w));
  Multiplexer multiplexer_7 (.sel(E[2]), .in_0(w), .in_1(E[4]), .out(multiplexer_7_out));
  D_FF d_ff_4 (.D(multiplexer_7_out), .C(w), .Q(Q4));  // open: nQ
  Multiplexer multiplexer_8 (.sel(LEFT), .in_0(E[3]), .in_1(Q3), .out(Q4));
  D_FF d_ff_5 (.D(multiplexer_10_out), .C(w), .Q(Q3));  // open: nQ
  Multiplexer multiplexer_9 (.sel(LEFT), .in_0(E[4]), .in_1(Q2), .out(Q3));
  Multiplexer multiplexer_10 (.sel(E[2]), .in_0(Q4), .in_1(E[3]), .out(multiplexer_10_out));
  D_FF d_ff_6 (.D(multiplexer_12_out), .C(w), .Q(Q2));  // open: nQ
  Multiplexer multiplexer_11 (.sel(LEFT), .in_0(E[5]), .in_1(Q1), .out(Q2));
  Multiplexer multiplexer_12 (.sel(E[2]), .in_0(Q3), .in_1(E[2]), .out(multiplexer_12_out));
  D_FF d_ff_7 (.D(multiplexer_14_out), .C(w), .Q(Q1));  // open: nQ
  Multiplexer multiplexer_13 (.sel(LEFT), .in_0(E[6]), .in_1(w), .out(Q1));
  Multiplexer multiplexer_14 (.sel(E[2]), .in_0(Q2), .in_1(E[1]), .out(multiplexer_14_out));
  Multiplexer multiplexer_15 (.sel(E[2]), .in_0(Q1), .in_1(E[0]), .out(multiplexer_15_out));
  D_FF d_ff_8 (.D(multiplexer_15_out), .C(w), .Q(w));  // open: nQ
  Multiplexer multiplexer_16 (.sel(LEFT), .in_0(E[7]), .in_1(1'b0), .out(multiplexer_16_out));

  assign Q0 = w;
  assign Q5 = w;
endmodule
