// Digital circuit multi 2.dig as structural Verilog
module multi_2 (
  input  A3,
  input  A2,
  input  A1,
  input  A0,
  input  B0,
  input  B1,
  input  B2,
  input  B3,
  input  W_op,
  input  cin,
  input  res,
  output S0,
  output S1,
  output S2,
  output S3,
  output S4,
  output S5,
  output S6,
  output S7
);

  wire add_8_bits__q3_2_1_s0, add_8_bits__q3_2_1_s1, add_8_bits__q3_2_1_s2, add_8_bits__q3_2_1_s3,
       add_8_bits__q3_2_1_s4, add_8_bits__q3_2_1_s5, add_8_bits__q3_2_1_s6, add_8_bits__q3_2_1_s7, and_1_out,
       \compteur_à_4_pour_multi_1_s0 , \compteur_à_4_pour_multi_1_s1 , not_1_out, or_1_out,
       registre_droit_4b_pour_q3_1_1_s0, \registre_à_gauche_8b_pour_q3_1_1_s0 ,
       \registre_à_gauche_8b_pour_q3_1_1_s1 , \registre_à_gauche_8b_pour_q3_1_1_s2 ,
       \registre_à_gauche_8b_pour_q3_1_1_s3 , \registre_à_gauche_8b_pour_q3_1_1_s4 ,
       \registre_à_gauche_8b_pour_q3_1_1_s5 , \registre_à_gauche_8b_pour_q3_1_1_s6 ,
       \registre_à_gauche_8b_pour_q3_1_1_s7 ;

  \compteur_à_4_pour_multi  \compteur_à_4_pour_multi_1  (
    .w(and_1_out), .res(res), .s0(\compteur_à_4_pour_multi_1_s0 ), .s1(\compteur_à_4_pour_multi_1_s1 ));
  or or_1 (or_1_out, \compteur_à_4_pour_multi_1_s0 , \compteur_à_4_pour_multi_1_s1 );
  D_FF d_ff_1 (.D(add_8_bits__q3_2_1_s7), .C(or_1_out), .Q(S7));  // open: nQ
  not not_1 (not_1_out, and_1_out);
  and and_1 (and_1_out, 1'b1, registre_droit_4b_pour_q3_1_1_s0);
  D_FF d_ff_2 (.D(add_8_bits__q3_2_1_s6), .C(or_1_out), .Q(S6));  // open: nQ
  Registre_droit_4b_pour_q3_1 registre_droit_4b_pour_q3_1_1 (
    .e0(B0), .e1(B1), .e2(B2), .e3(B3), .DEC(not_1_out), .w(W_op), .S0(registre_droit_4b_pour_q3_1_1_s0));  // open: S1, S2, S3
  D_FF d_ff_3 (.D(add_8_bits__q3_2_1_s5), .C(or_1_out), .Q(S5));  // open: nQ
  D_FF d_ff_4 (.D(add_8_bits__q3_2_1_s4), .C(or_1_out), .Q(S4));  // open: nQ
  D_FF d_ff_5 (.D(add_8_bits__q3_2_1_s3), .C(or_1_out), .Q(S3));  // open: nQ
  D_FF d_ff_6 (.D(add_8_bits__q3_2_1_s2), .C(or_1_out), .Q(S2));  // open: nQ
  ADD_8_bits__q3_2 add_8_bits__q3_2_1 (
    .A0(S0), .B0(\registre_à_gauche_8b_pour_q3_1_1_s0 ), .A1(S1), .B1(\registre_à_gauche_8b_pour_q3_1_1_s1 ),
    .A2(S2), .B2(\registre_à_gauche_8b_pour_q3_1_1_s2 ), .A3(S3), .B3(\registre_à_gauche_8b_pour_q3_1_1_s3 ),
    .Cin(cin), .A4(S4), .A5(S5), .A6(S6), .A7(S7), .B4(\registre_à_gauche_8b_pour_q3_1_1_s4 ),
    .B5(\registre_à_gauche_8b_pour_q3_1_1_s5 ), .B6(\registre_à_gauche_8b_pour_q3_1_1_s6 ),
    .B7(\registre_à_gauche_8b_pour_q3_1_1_s7 ), .S0(add_8_bits__q3_2_1_s0), .S1(add_8_bits__q3_2_1_s1),
    .S2(add_8_bits__q3_2_1_s2), .S3(add_8_bits__q3_2_1_s3), .S4(add_8_bits__q3_2_1_s4),
    .S5(add_8_bits__q3_2_1_s5), .S6(add_8_bits__q3_2_1_s6), .S7(add_8_bits__q3_2_1_s7));  // open: Cout
  D_FF d_ff_7 (.D(add_8_bits__q3_2_1_s1), .C(or_1_out), .Q(S1));  // open: nQ
  \Registre_à_gauche_8b_pour_q3_1  \registre_à_gauche_8b_pour_q3_1_1  (
    .e0(1'b0), .e1(1'b0), .e2(1'b0), .e3(1'b0), .e4(A0), .e5(A1), .e6(A2), .e7(A3), .DEC(not_1_out),
    .w(W_op), .S0(\registre_à_gauche_8b_pour_q3_1_1_s0 ), .S1(\registre_à_gauche_8b_pour_q3_1_1_s1 ),
    .S2(\registre_à_gauche_8b_pour_q3_1_1_s2 ), .S3(\registre_à_gauche_8b_pour_q3_1_1_s3 ),
    .S4(\registre_à_gauche_8b_pour_q3_1_1_s4 ), .S5(\registre_à_gauche_8b_pour_q3_1_1_s5 ),
    .S6(\registre_à_gauche_8b_pour_q3_1_1_s6 ), .S7(\registre_à_gauche_8b_pour_q3_1_1_s7 ));
  D_FF d_ff_8 (.D(add_8_bits__q3_2_1_s0), .C(or_1_out), .Q(S0));  // open: nQ
endmodule
