// Digital circuit mux 2 input.dig as structural Verilog
module mux_2_input (
  input  a1,
  input  a0,
  input  S,
  output out
);

  wire and_1_out, and_2_out, not_1_out;

  not not_1 (not_1_out, S);
  and and_1 (and_1_out, a0, S);
  and and_2 (and_2_out, a1, not_1_out);
  or or_1 (out, and_1_out, and_2_out);
endmodule
