// Digital circuit 999.dig as structural Verilog
module _999 (
  input  A0,
  input  A1,
  input  A2,
  input  A3,
  input  _0,
  input  S,
  output Y0,
  output Y1,
  output Y2,
  output Y3
);

  mux_2_input mux_2_input_1 (.a1(A3), .a0(A2), .S(S), .out(Y3));
  mux_2_input mux_2_input_2 (.a1(A2), .a0(A1), .S(S), .out(Y2));
  mux_2_input mux_2_input_3 (.a1(A1), .a0(A0), .S(S), .out(Y1));
  mux_2_input mux_2_input_4 (.a1(A0), .a0(_0), .S(S), .out(Y0));
endmodule
