// Digital circuit ADD 1 bit (q3.1).dig as structural Verilog
module ADD_1_bit__q3_1 (
  input  A0,
  input  A1,
  input  Cin,
  output S,
  output Cout
);

  wire and_1_out, and_2_out, xor_1_out, xor_2_out;

  xor xor_1 (xor_1_out, A0, A1);
  xor xor_2 (xor_2_out, A0, A1);
  xor xor_3 (S, xor_1_out, Cin);
  and and_1 (and_1_out, A0, A1);
  and and_2 (and_2_out, xor_2_out, Cin);
  or or_1 (Cout, and_1_out, and_2_out);
endmodule
