// Digital circuit ADD 8 bits (q3.2).dig as structural Verilog
module ADD_8_bits__q3_2 (
  input  A0,
  input  B0,
  input  A1,
  input  B1,
  input  A2,
  input  B2,
  input  A3,
  input  B3,
  input  Cin,
  input  A4,
  input  A5,
  input  A6,
  input  A7,
  input  B4,
  input  B5,
  input  B6,
  input  B7,
  output Cout,
  output S0,
  output S1,
  output S2,
  output S3,
  output S4,
  output S5,
  output S6,
  output S7
);

  wire add_1_bit__q3_1_2_cout, add_1_bit__q3_1_3_cout, add_1_bit__q3_1_4_cout, add_1_bit__q3_1_5_cout,
       add_1_bit__q3_1_6_cout, add_1_bit__q3_1_7_cout, add_1_bit__q3_1_8_cout;

  ADD_1_bit__q3_1 add_1_bit__q3_1_1 (.A0(A7), .A1(B7), .Cin(add_1_bit__q3_1_2_cout), .S(S7), .Cout(Cout));
  ADD_1_bit__q3_1 add_1_bit__q3_1_2 (
    .A0(A6), .A1(B6), .Cin(add_1_bit__q3_1_3_cout), .S(S6), .Cout(add_1_bit__q3_1_2_cout));
  ADD_1_bit__q3_1 add_1_bit__q3_1_3 (
    .A0(A5), .A1(B5), .Cin(add_1_bit__q3_1_4_cout), .S(S5), .Cout(add_1_bit__q3_1_3_cout));
  ADD_1_bit__q3_1 add_1_bit__q3_1_4 (
    .A0(A4), .A1(B4), .Cin(add_1_bit__q3_1_5_cout), .S(S4), .Cout(add_1_bit__q3_1_4_cout));
  ADD_1_bit__q3_1 add_1_bit__q3_1_5 (
    .A0(A3), .A1(B3), .Cin(add_1_bit__q3_1_6_cout), .S(S3), .Cout(add_1_bit__q3_1_5_cout));
  ADD_1_bit__q3_1 add_1_bit__q3_1_6 (
    .A0(A2), .A1(B2), .Cin(add_1_bit__q3_1_7_cout), .S(S2), .Cout(add_1_bit__q3_1_6_cout));
  ADD_1_bit__q3_1 add_1_bit__q3_1_7 (
    .A0(A1), .A1(B1), .Cin(add_1_bit__q3_1_8_cout), .S(S1), .Cout(add_1_bit__q3_1_7_cout));
  ADD_1_bit__q3_1 add_1_bit__q3_1_8 (.A0(A0), .A1(B0), .Cin(Cin), .S(S0), .Cout(add_1_bit__q3_1_8_cout));
endmodule
