// Digital circuit ADD SUB 8 bits.dig as structural Verilog
module ADD_SUB_8_bits (
  input  Sub,
  input  [7:0] B,
  input  [7:0] A,
  output Cout,
  output S0,
  output S1,
  output S2,
  output S3,
  output S4,
  output S5,
  output S6,
  output S7
);

  wire add_1_bit__q3_1_2_cout, add_1_bit__q3_1_3_cout, add_1_bit__q3_1_4_cout, add_1_bit__q3_1_5_cout,
       add_1_bit__q3_1_6_cout, add_1_bit__q3_1_7_cout, add_1_bit__q3_1_8_cout, xor_1_out, xor_2_out,
       xor_3_out, xor_4_out, xor_5_out, xor_6_out, xor_7_out, xor_8_out;

  xor xor_1 (xor_1_out, Sub, B[7]);
  ADD_1_bit__q3_1 add_1_bit__q3_1_1 (.A0(A[7]), .A1(xor_1_out), .Cin(add_1_bit__q3_1_2_cout), .S(S7), .Cout(Cout));
  xor xor_2 (xor_2_out, Sub, B[6]);
  ADD_1_bit__q3_1 add_1_bit__q3_1_2 (
    .A0(A[6]), .A1(xor_2_out), .Cin(add_1_bit__q3_1_3_cout), .S(S6), .Cout(add_1_bit__q3_1_2_cout));
  xor xor_3 (xor_3_out, Sub, B[5]);
  ADD_1_bit__q3_1 add_1_bit__q3_1_3 (
    .A0(A[5]), .A1(xor_3_out), .Cin(add_1_bit__q3_1_4_cout), .S(S5), .Cout(add_1_bit__q3_1_3_cout));
  xor xor_4 (xor_4_out, Sub, B[4]);
  ADD_1_bit__q3_1 add_1_bit__q3_1_4 (
    .A0(A[4]), .A1(xor_4_out), .Cin(add_1_bit__q3_1_5_cout), .S(S4), .Cout(add_1_bit__q3_1_4_cout));
  xor xor_5 (xor_5_out, Sub, B[3]);
  ADD_1_bit__q3_1 add_1_bit__q3_1_5 (
    .A0(A[3]), .A1(xor_5_out), .Cin(add_1_bit__q3_1_6_cout), .S(S3), .Cout(add_1_bit__q3_1_5_cout));
  xor xor_6 (xor_6_out, Sub, B[2]);
  ADD_1_bit__q3_1 add_1_bit__q3_1_6 (
    .A0(A[2]), .A1(xor_6_out), .Cin(add_1_bit__q3_1_7_cout), .S(S2), .Cout(add_1_bit__q3_1_6_cout));
  xor xor_7 (xor_7_out, Sub, B[1]);
  ADD_1_bit__q3_1 add_1_bit__q3_1_7 (
    .A0(A[1]), .A1(xor_7_out), .Cin(add_1_bit__q3_1_8_cout), .S(S1), .Cout(add_1_bit__q3_1_7_cout));
  xor xor_8 (xor_8_out, Sub, B[0]);
  ADD_1_bit__q3_1 add_1_bit__q3_1_8 (.A0(A[0]), .A1(xor_8_out), .Cin(Sub), .S(S0), .Cout(add_1_bit__q3_1_8_cout));
endmodule
