// Digital circuit CC 1 bit.dig as structural Verilog
module CC_1_bit (
  input  G,
  input  P,
  input  Cin,
  output Cout
);

  wire and_1_out, and_2_out, xor_1_out;

  xor xor_1 (xor_1_out, P, G);
  and and_1 (and_1_out, P, G);
  and and_2 (and_2_out, xor_1_out, Cin);
  or or_1 (Cout, and_1_out, and_2_out);
endmodule
