// Digital circuit DECAL A  GAUCHE.dig as structural Verilog
module DECAL_A__GAUCHE (
  input  [7:0] E,
  input  DEC,
  input  w,
  input  [7:0] LEFT,
  output [7:0] S
);

  wire and_1_out, registre__q_1_1_1_q0, registre__q_1_1_1_q1, registre__q_1_1_1_q2, registre__q_1_1_1_q3,
       registre__q_1_1_1_q4, registre__q_1_1_1_q5, registre__q_1_1_1_q6, registre__q_1_1_1_q7,
       registre__q_1_1_2_q0, registre__q_1_1_2_q1, registre__q_1_1_2_q2, registre__q_1_1_2_q3,
       registre__q_1_1_2_q4, registre__q_1_1_2_q5, registre__q_1_1_2_q6, registre__q_1_1_2_q7,
       registre__q_1_1_3_q0, registre__q_1_1_3_q1, registre__q_1_1_3_q2, registre__q_1_1_3_q3,
       registre__q_1_1_3_q4, registre__q_1_1_3_q5, registre__q_1_1_3_q6, registre__q_1_1_3_q7,
       registre__q_1_1_4_q0, registre__q_1_1_4_q1, registre__q_1_1_4_q2, registre__q_1_1_4_q3,
       registre__q_1_1_4_q4, registre__q_1_1_4_q5, registre__q_1_1_4_q6, registre__q_1_1_4_q7,
       registre__q_1_1_5_q0, registre__q_1_1_5_q1, registre__q_1_1_5_q2, registre__q_1_1_5_q3,
       registre__q_1_1_5_q4, registre__q_1_1_5_q5, registre__q_1_1_5_q6, registre__q_1_1_5_q7,
       registre__q_1_1_6_q0, registre__q_1_1_6_q1, registre__q_1_1_6_q2, registre__q_1_1_6_q3,
       registre__q_1_1_6_q4, registre__q_1_1_6_q5, registre__q_1_1_6_q6, registre__q_1_1_6_q7,
       registre__q_1_1_7_q0, registre__q_1_1_7_q1, registre__q_1_1_7_q2, registre__q_1_1_7_q3,
       registre__q_1_1_7_q4, registre__q_1_1_7_q5, registre__q_1_1_7_q6, registre__q_1_1_7_q7;

  and and_1 (and_1_out, DEC, w);
  Registre__q_1_1 registre__q_1_1_1 (
    .D0(E[0]), .D1(E[1]), .D2(E[2]), .D3(E[3]), .D4(E[4]), .D5(E[5]), .D6(E[6]), .D7(E[7]), .CLK(and_1_out),
    .Q0(registre__q_1_1_1_q0), .Q1(registre__q_1_1_1_q1), .Q2(registre__q_1_1_1_q2),
    .Q3(registre__q_1_1_1_q3), .Q4(registre__q_1_1_1_q4), .Q5(registre__q_1_1_1_q5),
    .Q6(registre__q_1_1_1_q6), .Q7(registre__q_1_1_1_q7));
  Registre__q_1_1 registre__q_1_1_2 (
    .D0(registre__q_1_1_1_q0), .D1(registre__q_1_1_1_q1), .D2(registre__q_1_1_1_q2),
    .D3(registre__q_1_1_1_q3), .D4(registre__q_1_1_1_q4), .D5(registre__q_1_1_1_q5),
    .D6(registre__q_1_1_1_q6), .D7(registre__q_1_1_1_q7), .CLK(and_1_out), .Q0(registre__q_1_1_2_q0),
    .Q1(registre__q_1_1_2_q1), .Q2(registre__q_1_1_2_q2), .Q3(registre__q_1_1_2_q3),
    .Q4(registre__q_1_1_2_q4), .Q5(registre__q_1_1_2_q5), .Q6(registre__q_1_1_2_q6), .Q7(registre__q_1_1_2_q7));
  Registre__q_1_1 registre__q_1_1_3 (
    .D0(registre__q_1_1_2_q0), .D1(registre__q_1_1_2_q1), .D2(registre__q_1_1_2_q2),
    .D3(registre__q_1_1_2_q3), .D4(registre__q_1_1_2_q4), .D5(registre__q_1_1_2_q5),
    .D6(registre__q_1_1_2_q6), .D7(registre__q_1_1_2_q7), .CLK(and_1_out), .Q0(registre__q_1_1_3_q0),
    .Q1(registre__q_1_1_3_q1), .Q2(registre__q_1_1_3_q2), .Q3(registre__q_1_1_3_q3),
    .Q4(registre__q_1_1_3_q4), .Q5(registre__q_1_1_3_q5), .Q6(registre__q_1_1_3_q6), .Q7(registre__q_1_1_3_q7));
  Registre__q_1_1 registre__q_1_1_4 (
    .D0(registre__q_1_1_3_q0), .D1(registre__q_1_1_3_q1), .D2(registre__q_1_1_3_q2),
    .D3(registre__q_1_1_3_q3), .D4(registre__q_1_1_3_q4), .D5(registre__q_1_1_3_q5),
    .D6(registre__q_1_1_3_q6), .D7(registre__q_1_1_3_q7), .CLK(and_1_out), .Q0(registre__q_1_1_4_q0),
    .Q1(registre__q_1_1_4_q1), .Q2(registre__q_1_1_4_q2), .Q3(registre__q_1_1_4_q3),
    .Q4(registre__q_1_1_4_q4), .Q5(registre__q_1_1_4_q5), .Q6(registre__q_1_1_4_q6), .Q7(registre__q_1_1_4_q7));
  Registre__q_1_1 registre__q_1_1_5 (
    .D0(registre__q_1_1_4_q0), .D1(registre__q_1_1_4_q1), .D2(registre__q_1_1_4_q2),
    .D3(registre__q_1_1_4_q3), .D4(registre__q_1_1_4_q4), .D5(registre__q_1_1_4_q5),
    .D6(registre__q_1_1_4_q6), .D7(registre__q_1_1_4_q7), .CLK(and_1_out), .Q0(registre__q_1_1_5_q0),
    .Q1(registre__q_1_1_5_q1), .Q2(registre__q_1_1_5_q2), .Q3(registre__q_1_1_5_q3),
    .Q4(registre__q_1_1_5_q4), .Q5(registre__q_1_1_5_q5), .Q6(registre__q_1_1_5_q6), .Q7(registre__q_1_1_5_q7));
  Registre__q_1_1 registre__q_1_1_6 (
    .D0(registre__q_1_1_5_q0), .D1(registre__q_1_1_5_q1), .D2(registre__q_1_1_5_q2),
    .D3(registre__q_1_1_5_q3), .D4(registre__q_1_1_5_q4), .D5(registre__q_1_1_5_q5),
    .D6(registre__q_1_1_5_q6), .D7(registre__q_1_1_5_q7), .CLK(and_1_out), .Q0(registre__q_1_1_6_q0),
    .Q1(registre__q_1_1_6_q1), .Q2(registre__q_1_1_6_q2), .Q3(registre__q_1_1_6_q3),
    .Q4(registre__q_1_1_6_q4), .Q5(registre__q_1_1_6_q5), .Q6(registre__q_1_1_6_q6), .Q7(registre__q_1_1_6_q7));
  Registre__q_1_1 registre__q_1_1_7 (
    .D0(registre__q_1_1_6_q0), .D1(registre__q_1_1_6_q1), .D2(registre__q_1_1_6_q2),
    .D3(registre__q_1_1_6_q3), .D4(registre__q_1_1_6_q4), .D5(registre__q_1_1_6_q5),
    .D6(registre__q_1_1_6_q6), .D7(registre__q_1_1_6_q7), .CLK(and_1_out), .Q0(registre__q_1_1_7_q0),
    .Q1(registre__q_1_1_7_q1), .Q2(registre__q_1_1_7_q2), .Q3(registre__q_1_1_7_q3),
    .Q4(registre__q_1_1_7_q4), .Q5(registre__q_1_1_7_q5), .Q6(registre__q_1_1_7_q6), .Q7(registre__q_1_1_7_q7));
  Registre__q_1_1 registre__q_1_1_8 (
    .D0(registre__q_1_1_7_q0), .D1(registre__q_1_1_7_q1), .D2(registre__q_1_1_7_q2),
    .D3(registre__q_1_1_7_q3), .D4(registre__q_1_1_7_q4), .D5(registre__q_1_1_7_q5),
    .D6(registre__q_1_1_7_q6), .D7(registre__q_1_1_7_q7), .CLK(and_1_out), .Q0(S[0]), .Q1(S[1]), .Q2(S[2]),
    .Q3(S[3]), .Q4(S[4]), .Q5(S[5]), .Q6(S[6]), .Q7(S[7]));
endmodule
