// Digital circuit OR BIN (q5.2).dig as structural Verilog
module OR_BIN__q5_2 (
  input  [7:0] A,
  input  [7:0] B,
  output S0,
  output S1,
  output S2,
  output S3,
  output S4,
  output S5,
  output S6,
  output S7
);

  assign {S7, S6, S5, S4, S3, S2, S1, S0} = A | B;  // Or or_1, 8 bits wide
endmodule
