// Digital circuit Registre a droite hehe raté (q.1.2).dig as structural Verilog
module \Registre_a_droite_hehe_raté__q_1_2  (
  input  [7:0] E,
  input  DEC,
  input  w,
  output Q0,
  output Q1,
  output Q2,
  output Q3,
  output Q4,
  output Q5,
  output Q6,
  output Q7
);

  wire multiplexer_1_out, multiplexer_2_out, multiplexer_3_out, multiplexer_4_out, multiplexer_5_out,
       multiplexer_6_out, multiplexer_7_out, multiplexer_8_out, not_1_out;

  Multiplexer multiplexer_1 (.sel(not_1_out), .in_0(1'b0), .in_1(E[7]), .out(multiplexer_1_out));
  not not_1 (not_1_out, DEC);
  D_FF d_ff_1 (.D(multiplexer_1_out), .C(w), .Q(Q7));  // open: nQ
  Multiplexer multiplexer_2 (.sel(not_1_out), .in_0(Q7), .in_1(E[6]), .out(multiplexer_2_out));
  D_FF d_ff_2 (.D(multiplexer_2_out), .C(w), .Q(Q6));  // open: nQ
  Multiplexer multiplexer_3 (.sel(not_1_out), .in_0(Q6), .in_1(E[5]), .out(multiplexer_3_out));
  D_FF d_ff_3 (.D(multiplexer_3_out), .C(w), .Q(Q5));  // open: nQ
  Multiplexer multiplexer_4 (.sel(not_1_out), .in_0(Q5), .in_1(E[4]), .out(multiplexer_4_out));
  D_FF d_ff_4 (.D(multiplexer_4_out), .C(w), .Q(Q4));  // open: nQ
  D_FF d_ff_5 (.D(multiplexer_5_out), .C(w), .Q(Q3));  // open: nQ
  Multiplexer multiplexer_5 (.sel(not_1_out), .in_0(Q4), .in_1(E[3]), .out(multiplexer_5_out));
  D_FF d_ff_6 (.D(multiplexer_6_out), .C(w), .Q(Q2));  // open: nQ
  Multiplexer multiplexer_6 (.sel(not_1_out), .in_0(Q3), .in_1(E[2]), .out(multiplexer_6_out));
  D_FF d_ff_7 (.D(multiplexer_7_out), .C(w), .Q(Q1));  // open: nQ
  Multiplexer multiplexer_7 (.sel(not_1_out), .in_0(Q2), .in_1(E[1]), .out(multiplexer_7_out));
  D_FF d_ff_8 (.D(multiplexer_8_out), .C(w), .Q(Q0));  // open: nQ
  Multiplexer multiplexer_8 (.sel(not_1_out), .in_0(Q1), .in_1(E[0]), .out(multiplexer_8_out));
endmodule
