// Digital circuit Registre droit 4b pour q3.1.dig as structural Verilog
module Registre_droit_4b_pour_q3_1 (
  input  e0,
  input  e1,
  input  e2,
  input  e3,
  input  DEC,
  input  w,
  output S0,
  output S1,
  output S2,
  output S3
);

  wire multiplexer_1_out, multiplexer_2_out, multiplexer_3_out, multiplexer_4_out, not_1_out;

  Multiplexer multiplexer_1 (.sel(not_1_out), .in_0(S1), .in_1(e0), .out(multiplexer_1_out));
  Multiplexer multiplexer_2 (.sel(not_1_out), .in_0(S2), .in_1(e1), .out(multiplexer_2_out));
  Multiplexer multiplexer_3 (.sel(not_1_out), .in_0(S3), .in_1(e2), .out(multiplexer_3_out));
  Multiplexer multiplexer_4 (.sel(not_1_out), .in_0(1'b0), .in_1(e3), .out(multiplexer_4_out));
  not not_1 (not_1_out, DEC);
  D_FF d_ff_1 (.D(multiplexer_1_out), .C(w), .Q(S0));  // open: nQ
  D_FF d_ff_2 (.D(multiplexer_2_out), .C(w), .Q(S1));  // open: nQ
  D_FF d_ff_3 (.D(multiplexer_3_out), .C(w), .Q(S2));  // open: nQ
  D_FF d_ff_4 (.D(multiplexer_4_out), .C(w), .Q(S3));  // open: nQ
endmodule
