// Digital circuit barrel shifter pro haha.dig as structural Verilog
module barrel_shifter_pro_haha (
  input  a0,
  input  a1,
  input  a2,
  input  a3,
  input  a4,
  input  a5,
  input  a6,
  input  a7,
  input  S,
  input  _0,
  input  S1,
  output Y0,
  output Y1,
  output Y2,
  output Y3,
  output Y4,
  output Y5,
  output Y6,
  output Y7
);

  wire mux_2_input_9_out, mux_2_input_10_out, mux_2_input_11_out, mux_2_input_12_out, mux_2_input_13_out,
       mux_2_input_14_out, mux_2_input_15_out, mux_2_input_16_out;

  mux_2_input mux_2_input_1 (.a1(_0), .a0(mux_2_input_9_out), .S(S1), .out(Y0));
  mux_2_input mux_2_input_2 (.a1(_0), .a0(mux_2_input_10_out), .S(S1), .out(Y1));
  mux_2_input mux_2_input_3 (.a1(mux_2_input_9_out), .a0(mux_2_input_11_out), .S(S1), .out(Y2));
  mux_2_input mux_2_input_4 (.a1(mux_2_input_10_out), .a0(mux_2_input_12_out), .S(S1), .out(Y3));
  mux_2_input mux_2_input_5 (.a1(mux_2_input_11_out), .a0(mux_2_input_13_out), .S(S1), .out(Y4));
  mux_2_input mux_2_input_6 (.a1(mux_2_input_12_out), .a0(mux_2_input_14_out), .S(S1), .out(Y5));
  mux_2_input mux_2_input_7 (.a1(mux_2_input_13_out), .a0(mux_2_input_15_out), .S(S1), .out(Y6));
  mux_2_input mux_2_input_8 (.a1(mux_2_input_14_out), .a0(mux_2_input_16_out), .S(S1), .out(Y7));
  mux_2_input mux_2_input_9 (.a1(_0), .a0(a0), .S(S), .out(mux_2_input_9_out));
  mux_2_input mux_2_input_10 (.a1(a0), .a0(a1), .S(S), .out(mux_2_input_10_out));
  mux_2_input mux_2_input_11 (.a1(a1), .a0(a2), .S(S), .out(mux_2_input_11_out));
  mux_2_input mux_2_input_12 (.a1(a2), .a0(a3), .S(S), .out(mux_2_input_12_out));
  mux_2_input mux_2_input_13 (.a1(a3), .a0(a4), .S(S), .out(mux_2_input_13_out));
  mux_2_input mux_2_input_14 (.a1(a4), .a0(a5), .S(S), .out(mux_2_input_14_out));
  mux_2_input mux_2_input_15 (.a1(a5), .a0(a6), .S(S), .out(mux_2_input_15_out));
  mux_2_input mux_2_input_16 (.a1(a6), .a0(a7), .S(S), .out(mux_2_input_16_out));
endmodule
