// Digital circuit compteur q2.11.dig as structural Verilog
module compteur_q2_11 (
  input  w,
  input  res,
  output s0,
  output s1,
  output s2
);

  wire and_1_out, and_2_out, and_3_out, and_4_out, not_1_out, not_2_out, xor_1_out, xor_2_out;

  and and_1 (and_1_out, s0, s1);
  not not_1 (not_1_out, res);
  not not_2 (not_2_out, s0);
  xor xor_1 (xor_1_out, s0, s1);
  xor xor_2 (xor_2_out, s2, and_1_out);
  D_FF d_ff_1 (.D(and_2_out), .C(w), .Q(s0));  // open: nQ
  D_FF d_ff_2 (.D(and_3_out), .C(w), .Q(s1));  // open: nQ
  D_FF d_ff_3 (.D(and_4_out), .C(w), .Q(s2));  // open: nQ
  and and_2 (and_2_out, not_2_out, not_1_out);
  and and_3 (and_3_out, xor_1_out, not_1_out);
  and and_4 (and_4_out, xor_2_out, not_1_out);
endmodule
