// Digital circuit multi 3.1.dig as structural Verilog
module multi_3_1 (
  input  A3,
  input  A2,
  input  A1,
  input  A0,
  input  B0,
  input  B1,
  input  B2,
  input  B3,
  input  CLK,
  input  res,
  output S0,
  output S1,
  output S2,
  output S3,
  output S4,
  output S5,
  output S6,
  output S7,
  output cout
);

  wire add_8_bits__q3_2_1_s0, add_8_bits__q3_2_1_s1, add_8_bits__q3_2_1_s2, add_8_bits__q3_2_1_s3,
       add_8_bits__q3_2_1_s4, add_8_bits__q3_2_1_s5, add_8_bits__q3_2_1_s6, add_8_bits__q3_2_1_s7, and_1_out,
       \compteur_à_4_pour_multi_1_s0 , \compteur_à_4_pour_multi_1_s1 , not_1_out, or_1_out,
       registre_droit_4b_pour_q3_1_1_s0;
  wire [7:0] multiplexer_1_out, \registre_à_gauche_8b_pour_q3_1_1_s7 ;

  \compteur_à_4_pour_multi  \compteur_à_4_pour_multi_1  (
    .w(CLK), .res(res), .s0(\compteur_à_4_pour_multi_1_s0 ), .s1(\compteur_à_4_pour_multi_1_s1 ));
  or or_1 (or_1_out, \compteur_à_4_pour_multi_1_s0 , \compteur_à_4_pour_multi_1_s1 );
  D_FF d_ff_1 (.D(add_8_bits__q3_2_1_s7), .C(or_1_out), .Q(S7));  // open: nQ
  Multiplexer #(.Bits(8)) multiplexer_1 (
    .sel(and_1_out), .in_0({8{1'b0}}), .in_1(\registre_à_gauche_8b_pour_q3_1_1_s7 ), .out(multiplexer_1_out));
  D_FF d_ff_2 (.D(add_8_bits__q3_2_1_s6), .C(or_1_out), .Q(S6));  // open: nQ
  D_FF d_ff_3 (.D(add_8_bits__q3_2_1_s5), .C(or_1_out), .Q(S5));  // open: nQ
  and and_1 (and_1_out, registre_droit_4b_pour_q3_1_1_s0, 1'b1);
  not not_1 (not_1_out, and_1_out);
  D_FF d_ff_4 (.D(add_8_bits__q3_2_1_s4), .C(or_1_out), .Q(S4));  // open: nQ
  Registre_droit_4b_pour_q3_1 registre_droit_4b_pour_q3_1_1 (
    .e0(B0), .e1(B1), .e2(B2), .e3(B3), .DEC(not_1_out), .w(not_1_out), .S0(registre_droit_4b_pour_q3_1_1_s0));  // open: S1, S2, S3
  D_FF d_ff_5 (.D(add_8_bits__q3_2_1_s3), .C(or_1_out), .Q(S3));  // open: nQ
  D_FF d_ff_6 (.D(add_8_bits__q3_2_1_s2), .C(or_1_out), .Q(S2));  // open: nQ
  ADD_8_bits__q3_2 add_8_bits__q3_2_1 (
    .A0(S0), .B0(multiplexer_1_out[0]), .A1(S1), .B1(multiplexer_1_out[1]), .A2(S2),
    .B2(multiplexer_1_out[2]), .A3(S3), .B3(multiplexer_1_out[3]), .Cin(1'b0), .A4(S4), .A5(S5), .A6(S6),
    .A7(S7), .B4(multiplexer_1_out[4]), .B5(multiplexer_1_out[5]), .B6(multiplexer_1_out[6]),
    .B7(multiplexer_1_out[7]), .Cout(cout), .S0(add_8_bits__q3_2_1_s0), .S1(add_8_bits__q3_2_1_s1),
    .S2(add_8_bits__q3_2_1_s2), .S3(add_8_bits__q3_2_1_s3), .S4(add_8_bits__q3_2_1_s4),
    .S5(add_8_bits__q3_2_1_s5), .S6(add_8_bits__q3_2_1_s6), .S7(add_8_bits__q3_2_1_s7));
  D_FF d_ff_7 (.D(add_8_bits__q3_2_1_s1), .C(or_1_out), .Q(S1));  // open: nQ
  \Registre_à_gauche_8b_pour_q3_1  \registre_à_gauche_8b_pour_q3_1_1  (
    .e0(1'b0), .e1(1'b0), .e2(1'b0), .e3(1'b0), .e4(A0), .e5(A1), .e6(A2), .e7(A3), .DEC(and_1_out),
    .w(and_1_out), .S0(\registre_à_gauche_8b_pour_q3_1_1_s7 [0]),
    .S1(\registre_à_gauche_8b_pour_q3_1_1_s7 [1]), .S2(\registre_à_gauche_8b_pour_q3_1_1_s7 [2]),
    .S3(\registre_à_gauche_8b_pour_q3_1_1_s7 [3]), .S4(\registre_à_gauche_8b_pour_q3_1_1_s7 [4]),
    .S5(\registre_à_gauche_8b_pour_q3_1_1_s7 [5]), .S6(\registre_à_gauche_8b_pour_q3_1_1_s7 [6]),
    .S7(\registre_à_gauche_8b_pour_q3_1_1_s7 [7]));
  D_FF d_ff_8 (.D(add_8_bits__q3_2_1_s0), .C(or_1_out), .Q(S0));  // open: nQ
endmodule
