// Digital circuit mux 8 input non récursif.dig as structural Verilog
module \mux_8_input_non_récursif  (
  input  y0,
  input  y2,
  input  y3,
  input  y4,
  input  y5,
  input  y6,
  input  y7,
  input  y1,
  input  Z0,
  input  Z1,
  input  Z2,
  output out
);

  wire and_1_out, and_2_out, and_3_out, and_4_out, and_5_out, and_6_out, and_7_out, and_8_out, deco_3_8_1_y0,
       deco_3_8_1_y1, deco_3_8_1_y2, deco_3_8_1_y3, deco_3_8_1_y4, deco_3_8_1_y5, deco_3_8_1_y6,
       deco_3_8_1_y7, or_1_out, or_2_out, or_3_out, or_4_out, or_5_out, or_6_out;

  deco_3_8 deco_3_8_1 (
    .e0(Z2), .e1(Z1), .e3(Z0), .y0(deco_3_8_1_y0), .y1(deco_3_8_1_y1), .y2(deco_3_8_1_y2),
    .y3(deco_3_8_1_y3), .y4(deco_3_8_1_y4), .y5(deco_3_8_1_y5), .y6(deco_3_8_1_y6), .y7(deco_3_8_1_y7));
  and and_1 (and_1_out, deco_3_8_1_y0, y0);
  and and_2 (and_2_out, deco_3_8_1_y1, y1);
  and and_3 (and_3_out, deco_3_8_1_y2, y2);
  and and_4 (and_4_out, deco_3_8_1_y3, y3);
  and and_5 (and_5_out, deco_3_8_1_y4, y4);
  and and_6 (and_6_out, deco_3_8_1_y5, y5);
  and and_7 (and_7_out, deco_3_8_1_y6, y6);
  and and_8 (and_8_out, deco_3_8_1_y7, y7);
  or or_1 (or_1_out, and_1_out, and_2_out);
  or or_2 (or_2_out, and_3_out, and_4_out);
  or or_3 (or_3_out, and_5_out, and_6_out);
  or or_4 (or_4_out, and_7_out, and_8_out);
  or or_5 (or_5_out, or_3_out, or_4_out);
  or or_6 (or_6_out, or_1_out, or_2_out);
  or or_7 (out, or_6_out, or_5_out);
endmodule
