// Digital circuit mux 8 inputs.dig as structural Verilog
module mux_8_inputs (
  input  y0,
  input  y2,
  input  y3,
  input  y4,
  input  y5,
  input  y6,
  input  y7,
  input  y1,
  input  Z0,
  input  Z1,
  input  Z2,
  output out
);

  wire mux_2_input_1_out, mux_2_input_2_out, mux_2_input_3_out, mux_2_input_5_out, mux_2_input_6_out,
       mux_2_input_7_out;

  mux_2_input mux_2_input_1 (.a1(y6), .a0(y7), .S(Z0), .out(mux_2_input_1_out));
  mux_2_input mux_2_input_2 (.a1(y4), .a0(y5), .S(Z0), .out(mux_2_input_2_out));
  mux_2_input mux_2_input_3 (.a1(mux_2_input_2_out), .a0(mux_2_input_1_out), .S(Z1), .out(mux_2_input_3_out));
  mux_2_input mux_2_input_4 (.a1(mux_2_input_6_out), .a0(mux_2_input_3_out), .S(Z2), .out(out));
  mux_2_input mux_2_input_5 (.a1(y2), .a0(y3), .S(Z0), .out(mux_2_input_5_out));
  mux_2_input mux_2_input_6 (.a1(mux_2_input_7_out), .a0(mux_2_input_5_out), .S(Z1), .out(mux_2_input_6_out));
  mux_2_input mux_2_input_7 (.a1(y0), .a0(y1), .S(Z0), .out(mux_2_input_7_out));
endmodule
